# Fritzing sketch heart (saved by Fritzing 0.9.6b)
breadboards: 1

parts:
  YwRobot_Power_Supply1 = YwRobot Breadboard Power Supply [part_number=545043]
  M1 = MakerFocus MAX30102
  U1 = ESP8266 ESP-01 Upgraded WiFi Module [part_number=ESP8266]

nets:
  VIN: YwRobot_Power_Supply1.VCC#5, YwRobot_Power_Supply1.VCC#6, M1.SCL, M1.VIN, U1.RXD, U1.VCC, U1.GPIO_2, U1.CH_PD
  N1: YwRobot_Power_Supply1.VCC#9, YwRobot_Power_Supply1.VCC#10
  GND: YwRobot_Power_Supply1.GND#11, YwRobot_Power_Supply1.GND#12, M1.GND, U1.GND, U1.TXD
  N2: YwRobot_Power_Supply1.GND#13, YwRobot_Power_Supply1.GND#14
  N3: M1.SDA, U1.GPIO_0, U1.RST/GPIO_16

custom parts:
  YwRobot Breadboard Power Supply: The YwRobot Breadboard Power Supply (MB-V2) has two power rails; they can be 5V or 3V3. Power to the module can be provided through the female USB socket or through the A10 (female) 2.1mm power jack.
  MakerFocus MAX30102: Oximeter module using the MAX30102 chip. As usual, if you want the mounting holes in pcb, you need to drag a hole over the pad in silkscreen to actually drill the hole (by default they are not drilled)
  ESP8266 ESP-01 Upgraded WiFi Module: Upgraded Version ESP-01,all Flash are upgraded to 1M byte.Also support Cloud service remote transmission.
