# Fritzing sketch motion (saved by Fritzing 0.9.6b)
breadboards: 1

parts:
  U1 = ESP8266 ESP-01 Upgraded WiFi Module [part_number=ESP8266]
  YwRobot_Power_Supply1 = YwRobot Breadboard Power Supply [part_number=545043]
  Part1 = Arduino Nano (Rev3.0)

nets:
  VCC: U1.VCC, U1.CH_PD, YwRobot_Power_Supply1.VCC#9, YwRobot_Power_Supply1.VCC#10, Part1.VIN
  N1: U1.GPIO_0, Part1.A4
  N2: U1.GPIO_2, Part1.A5
  GND: U1.GND, YwRobot_Power_Supply1.GND#13, YwRobot_Power_Supply1.GND#14, Part1.GND
  N3: YwRobot_Power_Supply1.VCC#5, YwRobot_Power_Supply1.VCC#6
  N4: YwRobot_Power_Supply1.GND#11, YwRobot_Power_Supply1.GND#12

custom parts:
  ESP8266 ESP-01 Upgraded WiFi Module: Upgraded Version ESP-01,all Flash are upgraded to 1M byte.Also support Cloud service remote transmission.
  YwRobot Breadboard Power Supply: The YwRobot Breadboard Power Supply (MB-V2) has two power rails; they can be 5V or 3V3. Power to the module can be provided through the female USB socket or through the A10 (female) 2.1mm power jack.
