# Fritzing sketch visualizer2 (saved by Fritzing 0.9.6b)
breadboards: 2

parts:
  LCD2 = LCD screen
  U1 = ESP32-38PinWide [part_number=ESP32-38PinWide]
  LCM1602_IIC1 = LCM1602 IIC [part_number="LCM1602 IIC" chip_label="LCM1602 IIC" package="DIP (Dual Inline) [THT]"]
  J2 = Basic Servo

nets:
  VSS: LCD2.VSS, LCM1602_IIC1.VSS
  VDD: LCD2.VDD, LCM1602_IIC1.VDD
  N1: LCD2.V0, LCM1602_IIC1.V0
  N2: LCD2.RS, LCM1602_IIC1.RS
  N3: LCD2.R/W, LCM1602_IIC1.RW
  N4: LCD2.E, LCM1602_IIC1.E
  N5: LCD2.DB0, LCM1602_IIC1.D0
  N6: LCD2.DB1, LCM1602_IIC1.D1
  N7: LCD2.DB2, LCM1602_IIC1.D2
  N8: LCD2.DB3, LCM1602_IIC1.D3
  N9: LCD2.DB4, LCM1602_IIC1.D4
  N10: LCD2.DB5, LCM1602_IIC1.D5
  N11: LCD2.DB6, LCM1602_IIC1.D6
  N12: LCD2.DB7, LCM1602_IIC1.D7
  N13: LCD2.LED+, LCM1602_IIC1.A
  N14: LCD2.LED-, LCM1602_IIC1.K
  N15: U1.GPIO12, J2.pulse
  GND: U1.GND, LCM1602_IIC1.GND, J2.gnd
  VCC: U1.VIN, LCM1602_IIC1.VCC, LCM1602_IIC1.LED_A, J2.vcc
  N16: U1.GPIO21, LCM1602_IIC1.SDA, LCM1602_IIC1.LED_B
  N17: U1.GPIO22, LCM1602_IIC1.SCL

custom parts:
  ESP32-38PinWide: Generic 38-Pin ESP32 with wide format (only access to one side of pins on a breadboard) based on Stephen Lilley's HiLetgo ESP-WROOM-32 ESP32 ESP-32S Development Board.
  LCM1602 IIC: I2C-Module to use a 1602 or 2004 LCD on with the wire.h libory Serial LCD Modul
